# Fritzing sketch v2-xmas-tree (saved by Fritzing 0.9.3b)
circuit board: 10cm x 20cm
breadboards: 1

parts:
  U1 = attiny85 [package=dip]
  LED2 = LED - 3mm [color="Green (555nm)" package="3 mm [THT]"]
  LED3 = LED - 3mm [color="Green (555nm)" package="3 mm [THT]"]
  LED4 = LED - 3mm [color="Green (555nm)" package="3 mm [THT]"]
  LED5 = LED - 3mm [color="Blue (430nm)" package="3 mm [THT]"]
  LED6 = LED - 3mm [color="Blue (430nm)" package="3 mm [THT]"]
  LED7 = LED - 3mm [color="Blue (430nm)" package="3 mm [THT]"]
  LED8 = LED - 3mm [color="Yellow (585nm)" package="3 mm [THT]"]
  LED9 = LED - 3mm [color="Yellow (585nm)" package="3 mm [THT]"]
  LED1 = LED - 3mm [color="White (4500K)" package="3 mm [THT]"]
  S1 = Pushbutton [package="[THT]"]
  VCC1 = Battery block 9V
  LED10 = LED - 3mm [color="Yellow (585nm)" package="3 mm [THT]"]
  R3 = Resistor [tolerance=±5% resistance=68 package=THT]
  R4 = Resistor [tolerance=±5% resistance=68 package=THT]
  R2 = Resistor [tolerance=±5% resistance=68 package=THT]
  R1 = Resistor [tolerance=±5% resistance=1k package=THT]
  R5 = Resistor [tolerance=±5% resistance=68 package=THT]

nets (from the schematic view):
  N1: U1.Pin_2, S1.Pin_3, S1.Pin_4, R2.Pin_1, R1.Pin_1
  N2: U1.Pin_4, LED2.cathode, LED3.cathode, LED4.cathode, LED5.cathode, LED6.cathode, LED7.cathode, LED8.cathode, LED9.cathode, LED1.cathode, VCC1.-, LED10.cathode, R1.Pin_0
  N3: U1.Pin_5, R3.Pin_1
  N4: U1.Pin_6, R4.Pin_1
  N5: U1.Pin_7, R5.Pin_1
  N6: U1.Pin_8, S1.Pin_1, S1.Pin_2, VCC1.+
  N7: LED2.anode, LED3.anode, LED4.anode, R5.Pin_0
  N8: LED5.anode, LED6.anode, LED7.anode, R4.Pin_0
  N9: LED8.anode, LED9.anode, LED10.anode, R3.Pin_0
  N10: LED1.anode, R2.Pin_0
